# Fritzing sketch MLTK01 (saved by Fritzing 0.9.3b)
breadboards: 1

parts:
  Part1 = Arduino Nano 33 BLE Sense
  Part2 = Logic Level Converter
  Part3 = NeoPixel Stick [part_number=1426]
  ENCODER2 = Rotary Encoder with Knob
  S1 = Momentary Switch [package=ksa_sealed_tac_switch]
  S2 = Toggle Switch [package=THT]

nets:
  GND: Part1.GND, Part1.A7, Part2.GND, Part3.GND, ENCODER2.no_name_yet#1, ENCODER2.no_name_yet#2, ENCODER2.no_name_yet#4, S1.3, S2.L2
  N1: Part1.D2, ENCODER2.no_name_yet#5
  N2: Part1.D3~, S1.1
  N3: Part1.D4, S2.COM
  N4: Part1.D5~, Part2.RX_LV
  +5V: Part1.D11/MOSI, Part1.+5V, Part2.HV, Part3.+5V
  N5: Part1.A6, ENCODER2.no_name_yet#3
  N6: Part1.AREF, Part2.LV, S2.L1

custom parts:
  Arduino Nano 33 BLE Sense: The Nano 33 BLE Sense (without headers) is Arduino’s 3.3V AI enabled board in the smallest available form factor: 45x18mm! The Arduino Nano 33 BLE Sense is a completely new board on a well-known form factor. It comes with a series of embedded sensors: 9 axis inertial sensor: what makes this board ideal for wearable devices humidity, and temperature sensor: to get highly accurate measurements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
  NeoPixel Stick: Make your own little LED strip arrangement with this stick of NeoPixel LEDs. We crammed 8 of the tiny 5050 (5mm x 5mm) smart RGB LEDs onto a PCB with mounting holes and a chainable design. Use only one microcontroller pin to control as many as you can chain together! Each LED is addressable as the driver chip is inside the LED. Each one has ~18mA constant current drive so the color will be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
  Rotary Encoder with Knob: Rotary Encoder with 1/4" Shaft and Knob
